# Fritzing sketch Schema_DHT11 (saved by Fritzing 0.9.0b)
breadboards: 1

parts:
  A1 = Arduino Uno (Rev3)
  C1 = Humidity and Temperature Sensor RHT03
  R1 = Resistor [tolerance=±5% resistance=1k package=THT]

nets (from the breadboard view):
  N1: A1.D5_PWM, C1.Data-signal, R1.Pin_0
  5V: A1.5V, C1.Vcc, R1.Pin_1
  N2: A1.GND, C1.GND_1
