# Fritzing sketch Schema_DS18B20 (saved by Fritzing 0.9.0b)
breadboards: 1

parts:
  A1 = Arduino Uno (Rev3)
  R1 = Resistor [tolerance=±5% resistance=4.7k package=THT]
  C1 = LM35 Temperature Sensor [package="TO92 [THT]"]

nets:
  N1: A1.D5_PWM, R1.Pin_0, C1.Vout
  N2: A1.5V, R1.Pin_1, C1.+Vs
  GND: A1.GND, C1.GND
