# Fritzing sketch Schema_LM35 (saved by Fritzing 0.9.0b)
breadboards: 1

parts:
  A1 = Arduino Uno (Rev3)
  C1 = LM35 Temperature Sensor [package="TO92 [THT]"]

nets:
  N1: A1.A0, C1.Vout
  N2: A1.5V, C1.+Vs
  GND: A1.GND, C1.GND
